# Fritzing sketch config-simple (saved by Fritzing 0.9.3b)

parts:
  WeMos_D1_Mini2 = WeMos D1 Mini
  J10 = Camdenboss CTB0158-8 [part_number=CTB0158-8 package=THT]  # not connected
  J9 = Camdenboss CTB0158-8 [part_number=CTB0158-8 package=THT]  # not connected
  J5 = Camdenboss CTB0158-8 [part_number=CTB0158-8 package=THT]
  J6 = Camdenboss CTB0158-8 [part_number=CTB0158-8 package=THT]
  J8 = Camdenboss CTB0158-8 [part_number=CTB0158-8 package=THT]
  J7 = Camdenboss CTB0158-8 [part_number=CTB0158-8 package=THT]

nets:
  N1: WeMos_D1_Mini2.D0, J6.terminal_2
  N2: WeMos_D1_Mini2.D1, J5.terminal_5
  N3: WeMos_D1_Mini2.D2, J6.terminal_4
  N4: WeMos_D1_Mini2.D3, J6.terminal_5
  N5: WeMos_D1_Mini2.D4, J5.terminal_8
  N6: WeMos_D1_Mini2.D5, J5.terminal_7
  N7: WeMos_D1_Mini2.D6, J6.terminal_3
  N8: WeMos_D1_Mini2.D7, J5.terminal_1
  N9: WeMos_D1_Mini2.D8, J5.terminal_6
  N10: J5.terminal_2, J7.terminal_6
  N11: J5.terminal_3, J8.terminal_1
  N12: J5.terminal_4, J8.terminal_2
  N13: J6.terminal_1, J7.terminal_1
  N14: J6.terminal_6, J7.terminal_8
  N15: J6.terminal_8, J8.terminal_3

notes:
  D4
  D5
  D8
  D1
  D7
  D3
  D2
  D6
  D0
  R0
  B0
  R1
  B1
  A
  C
  CLK
  OE
  GND
  GND(or E)
  B
  GND(or D)
  STB
  IN
  OUT
