# Fritzing sketch config (saved by Fritzing 0.9.3b)

parts:
  WeMos_D1_Mini2 = WeMos D1 Mini
  SW1 = DIP Switch 8 Position [package=dipswitch-08]
  SW2 = DIP Switch 8 Position [package=dipswitch-08]
  J1 = Camdenboss CTB0158-8 [part_number=CTB0158-8 package=THT]
  J2 = Camdenboss CTB0158-8 [part_number=CTB0158-8 package=THT]
  J3 = Camdenboss CTB0158-8 [part_number=CTB0158-8 package=THT]
  J4 = Camdenboss CTB0158-8 [part_number=CTB0158-8 package=THT]
  J11 = Camdenboss CTB0158-8 [part_number=CTB0158-8 package=THT]  # not connected
  J12 = Camdenboss CTB0158-8 [part_number=CTB0158-8 package=THT]  # not connected
  J13 = Camdenboss CTB0158-8 [part_number=CTB0158-8 package=THT]  # not connected
  J14 = Camdenboss CTB0158-8 [part_number=CTB0158-8 package=THT]  # not connected

nets:
  N1: WeMos_D1_Mini2.D0, SW1.1
  N2: WeMos_D1_Mini2.D1, SW2.6
  N3: WeMos_D1_Mini2.D2, SW2.5
  N4: WeMos_D1_Mini2.D3, SW2.4
  N5: WeMos_D1_Mini2.D4, SW2.3
  N6: WeMos_D1_Mini2.D5, SW1.2
  N7: WeMos_D1_Mini2.D6, SW1.3
  N8: WeMos_D1_Mini2.D7, SW1.4
  N9: WeMos_D1_Mini2.D8, SW1.5
  N10: SW1.12, J1.pin6
  N11: SW1.13, J1.pin1
  N12: SW1.14, J2.pin3
  N13: SW1.15, J1.pin7
  N14: SW1.16, J2.pin2
  N15: SW2.11, J1.pin5
  N16: SW2.12, J2.pin4
  N17: SW2.13, J2.pin5
  N18: SW2.14, J1.pin8
  N19: J1.terminal_2, J4.terminal_6
  N20: J1.terminal_3, J3.terminal_1
  N21: J1.terminal_4, J3.terminal_2
  N22: J2.terminal_1, J4.terminal_1
  N23: J2.terminal_6, J4.terminal_8
  N24: J2.terminal_8, J3.terminal_3

notes:
  GND(or D)
  GND(or E)
  C
  R0
  B1
  R1
  OE
  B0
  CLK
  GND
  STB
  A
  B
  OUT
  IN
